# Fritzing sketch vbox (saved by Fritzing 0.9.6b)

parts:
  Componente1 = LCD1602-I2C
  A1 = AHT10 module
  Part4 = Barometric Pressure Sensor - BMP180 Breakout (GY-68)
  Mod1 = MQ-5_1
  Chirp!_Soil_Moisture_Sensor1 = Chirp! Soil Moisture Sensor v2.7.3  # not connected
  LED1 = RGB LED (com. cathode, rgb) [package="5 mm [THT]"]
  Mod2 = Raspberry Pi 4B  # not connected
  M1 = esp32_p30_w11 [part_number=ESP32S-PIN30]

nets:
  GND: Componente1.GND, A1.Pin_2, Part4.GND, Mod1.connector1, LED1.common_cathode, M1.connector28
  VCC: Componente1.VCC, A1.Pin_1, Part4.VCC, Mod1.connector0, M1.connector29
  N1: Componente1.SDA, A1.Pin_4, Part4.SDA, M1.connector10
  N2: Componente1.SCL, A1.Pin_3, Part4.SCL, M1.connector13
  N3: Mod1.connector3, M1.connector19
  N4: LED1.red_anode, M1.connector27
  N5: LED1.green_anode, M1.connector26
  N6: LED1.blue_anode, M1.connector25

custom parts:
  LCD1602-I2C: A standard character display, usually with 2x16 characters. Comes in many colors with LCM1602 IIC attached.
  AHT10 module: AHT10 Temperature Humidity Sensor Measurement Module High-Precision Digital Temp Humidity Sensor Measurement Module 1.8-6.0V I2C.
